# Fritzing sketch evpr_fritzing (saved by Fritzing 0.9.3b)
perfboards: 1

parts:
  SparkFun_ESP32_Thing1 = SparkFun ESP32 Thing [part_number=DEV-13907]
  U1 = LIPO-1000mAh [package=lipo-1000]
  U2 = LIPO-1000mAh [package=lipo-1000]
  J2 = screw terminal, 4 pins
  J3 = Basic Servo
  J4 = Basic Servo
  J6 = screw terminal, 3 pins
  U3 = SWITCH_SPDT [package=kps-1290]
  U4 = Voltage Regulator - 5V [package="DPak [SMD]"]
  C2 = Tantalum Capacitor [capacitance="1 μF" package="A 3216 [SMD, tantalum]"]
  C3 = Tantalum Capacitor [capacitance="1 μF" package="A 3216 [SMD, tantalum]"]
  J5 = screw terminal, 3 pins

nets:
  N1: SparkFun_ESP32_Thing1.VUSB-RAW, U4.output_voltage, C3.+
  GND: SparkFun_ESP32_Thing1.GND, U2.-, J2.pin1, J3.gnd, U4.GND, C2.-, C3.-, J5.pin3
  N2: SparkFun_ESP32_Thing1.16, J3.pulse, J5.pin1
  N3: SparkFun_ESP32_Thing1.17, J4.pulse, J6.pin1
  N4: U1.+, J2.pin4, U3.P
  N5: U1.-, U2.+, J2.pin2, J2.pin3
  VCC: J3.vcc, J4.vcc, J6.pin2, U3.S, U4.input_voltage, C2.+, J5.pin2
  N6: J4.gnd, J6.pin3

custom parts:
  SparkFun ESP32 Thing: The SparkFun ESP32 Thing is a comprehensive development platform for Espressif’s ESP32, their super-charged version of the popular ESP8266. Like the 8266, the ESP32 is a WiFi-compatible microcontroller, but to that it adds support for Bluetooth low-energy (i.e BLE, BT4.0, Bluetooth Smart), and nearly 30 I/O pins. The ESP32’s power and versatility will make it the foundation of IoT and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
